// Logisim project Lift.circ as structural Verilog
module lIFT (
  input  [3:0] ETAJ,
  input  Persoana_in_usa,
  input  Greutate_depasita,
  input  Cerere_int,
  input  Cerere_ext_sus,
  input  Cerere_ext_jos,
  input  Load,
  input  CLK,
  output [7:0] Output_bus_1,
  output [6:0] Output_bus_2
);

  wire divizor_frecventa_1_clk_1hz, mux_16_1_1_y, mux_16_1_2_y, mux_16_1_3_y, numarator_3s_1_carry,
       numarator_12_1_carry, numarator_inchidere_usa_1_carry, poarta_nor_3in_13b_1_y, poarta_or_1_y,
       unitate_de_control_1_dir, unitate_de_control_1_en_exterior_jos, unitate_de_control_1_en_exterior_sus,
       unitate_de_control_1_en_interior, unitate_de_control_1_enable_inchidere_usa,
       unitate_de_control_1_load_registrii;
  wire [3:0] afisare_etaje_1_c1, afisare_etaje_1_c2, numarator_12_1_count, unitate_de_control_1_etaj_cerut;
  wire [12:0] registru_de_memorare_1_y, registru_de_memorare_2_y, registru_de_memorare_3_y;

  LED Deschidere_usa (.in(poarta_or_1_y));
  LED Usa_inchisa (.in(numarator_inchidere_usa_1_carry));
  LED Mers_intre_etaje (.in(numarator_3s_1_carry));
  LED Ajungere_Etaj (.in(poarta_or_1_y));
  LED Greutate_inco (.in(Greutate_depasita));
  LED Pers_in_usa (.in(Persoana_in_usa));
  divizor_frecventa divizor_frecventa_1 (.Clk_100(CLK), .Clk_1Hz(divizor_frecventa_1_clk_1hz));
  UNITATE_DE_CONTROL unitate_de_control_1 (
    .ETAJ(ETAJ), .PERSOANA_IN_USA(Persoana_in_usa), .GREUTEATE_DEPASITA(Greutate_depasita),
    .INTERIOR(Cerere_int), .EXTERIOR_SUS(Cerere_ext_sus), .EXTERIOR_JOS(Cerere_ext_jos), .OK(Load),
    .FARA_CERERI(poarta_nor_3in_13b_1_y), .CLK(divizor_frecventa_1_clk_1hz), .RESET(poarta_or_1_y),
    .RESET_DIR(numarator_12_1_carry), .DIR(unitate_de_control_1_dir),
    .ENABLE_INCHIDERE_USA(unitate_de_control_1_enable_inchidere_usa),
    .LOAD_REGISTRII(unitate_de_control_1_load_registrii), .EN_INTERIOR(unitate_de_control_1_en_interior),
    .EN_EXTERIOR_SUS(unitate_de_control_1_en_exterior_sus),
    .EN_EXTERIOR_JOS(unitate_de_control_1_en_exterior_jos), .ETAJ_CERUT(unitate_de_control_1_etaj_cerut));
  Numarator_inchidere_usa numarator_inchidere_usa_1 (
    .CLK(divizor_frecventa_1_clk_1hz), .RESET(poarta_or_1_y), .EN(unitate_de_control_1_enable_inchidere_usa),
    .CARRY(numarator_inchidere_usa_1_carry));
  Numarator_3s numarator_3s_1 (
    .CLK(divizor_frecventa_1_clk_1hz), .EN(numarator_inchidere_usa_1_carry), .CARRY(numarator_3s_1_carry));
  afisare afisare_1 (
    .clk_100(CLK), .reset(poarta_or_1_y), .I0(afisare_etaje_1_c1), .I1(afisare_etaje_1_c2),
    .anozi(Output_bus_1[0]), .catozi(Output_bus_2));
  AFISARE_ETAJE afisare_etaje_1 (.ETAJ(numarator_12_1_count), .C1(afisare_etaje_1_c1), .C2(afisare_etaje_1_c2));
  Numarator_12 numarator_12_1 (
    .CLK(divizor_frecventa_1_clk_1hz), .EN(numarator_3s_1_carry), .DIR(unitate_de_control_1_dir),
    .CARRY(numarator_12_1_carry), .COUNT(numarator_12_1_count));
  Registru_de_memorare registru_de_memorare_1 (
    .Load(unitate_de_control_1_load_registrii), .R(unitate_de_control_1_enable_inchidere_usa),
    .En(unitate_de_control_1_en_interior), .reset(numarator_12_1_count), .Q(unitate_de_control_1_etaj_cerut),
    .Y(registru_de_memorare_1_y));
  Registru_de_memorare registru_de_memorare_2 (
    .Load(unitate_de_control_1_load_registrii), .R(unitate_de_control_1_enable_inchidere_usa),
    .En(unitate_de_control_1_en_exterior_sus), .reset(numarator_12_1_count),
    .Q(unitate_de_control_1_etaj_cerut), .Y(registru_de_memorare_2_y));
  Registru_de_memorare registru_de_memorare_3 (
    .Load(unitate_de_control_1_load_registrii), .R(unitate_de_control_1_enable_inchidere_usa),
    .En(unitate_de_control_1_en_exterior_jos), .reset(numarator_12_1_count),
    .Q(unitate_de_control_1_etaj_cerut), .Y(registru_de_memorare_3_y));
  MUX_16_1 mux_16_1_1 (
    .C0(registru_de_memorare_1_y[0]), .C1(registru_de_memorare_1_y[1]), .C2(registru_de_memorare_1_y[2]),
    .C3(registru_de_memorare_1_y[3]), .C4(registru_de_memorare_1_y[4]), .C5(registru_de_memorare_1_y[5]),
    .C6(registru_de_memorare_1_y[6]), .C7(registru_de_memorare_1_y[7]), .C8(registru_de_memorare_1_y[8]),
    .C9(registru_de_memorare_1_y[9]), .C10(registru_de_memorare_1_y[10]), .C11(registru_de_memorare_1_y[11]),
    .C12(registru_de_memorare_1_y[12]), .C13(1'b0), .C14(1'b0), .C15(1'b0), .SEL(numarator_12_1_count),
    .Y(mux_16_1_1_y));
  MUX_16_1 mux_16_1_2 (
    .C0(registru_de_memorare_2_y[0]), .C1(registru_de_memorare_2_y[1]), .C2(registru_de_memorare_2_y[2]),
    .C3(registru_de_memorare_2_y[3]), .C4(registru_de_memorare_2_y[4]), .C5(registru_de_memorare_2_y[5]),
    .C6(registru_de_memorare_2_y[6]), .C7(registru_de_memorare_2_y[7]), .C8(registru_de_memorare_2_y[8]),
    .C9(registru_de_memorare_2_y[9]), .C10(registru_de_memorare_2_y[10]), .C11(registru_de_memorare_2_y[11]),
    .C12(registru_de_memorare_2_y[12]), .C13(1'b0), .C14(1'b0), .C15(1'b0), .SEL(numarator_12_1_count),
    .Y(mux_16_1_2_y));
  MUX_16_1 mux_16_1_3 (
    .C0(registru_de_memorare_3_y[0]), .C1(registru_de_memorare_3_y[1]), .C2(registru_de_memorare_3_y[2]),
    .C3(registru_de_memorare_3_y[3]), .C4(registru_de_memorare_3_y[4]), .C5(registru_de_memorare_3_y[5]),
    .C6(registru_de_memorare_3_y[6]), .C7(registru_de_memorare_3_y[7]), .C8(registru_de_memorare_3_y[8]),
    .C9(registru_de_memorare_3_y[9]), .C10(registru_de_memorare_3_y[10]), .C11(registru_de_memorare_3_y[11]),
    .C12(registru_de_memorare_3_y[12]), .C13(1'b0), .C14(1'b0), .C15(1'b0), .SEL(numarator_12_1_count),
    .Y(mux_16_1_3_y));
  Poarta_or poarta_or_1 (.A(mux_16_1_1_y), .B(mux_16_1_2_y), .C(mux_16_1_3_y), .Y(poarta_or_1_y));
  Poarta_NOR_3In_13B poarta_nor_3in_13b_1 (
    .A(registru_de_memorare_1_y), .B(registru_de_memorare_2_y), .C(registru_de_memorare_3_y),
    .CLK(divizor_frecventa_1_clk_1hz), .Y(poarta_nor_3in_13b_1_y));
  // Pins of 1 and 8 bits meet at Output_bus_1
endmodule

// VHDL entity Numarator_12, as the project stores it:
LIBRARY ieee;
USE ieee.std_logic_1164.all;
USE IEEE.STD_LOGIC_UNSIGNED.ALL;

ENTITY Numarator_12 IS
  PORT (CLK:IN STD_LOGIC;
  	    EN,DIR: IN STD_LOGIC;
  	    CARRY: OUT STD_LOGIC;
  	    COUNT: OUT STD_LOGIC_VECTOR(3 DOWNTO 0));
END Numarator_12;
ARCHITECTURE ArchNumarator_12 OF Numarator_12 IS
SIGNAL TMP: STD_LOGIC_VECTOR(3 DOWNTO 0):=(OTHERS => '0');
SIGNAL F: STD_LOGIC;

BEGIN
   PROCESS(CLK)
      BEGIN
         IF RISING_EDGE(CLK) THEN
               IF (EN='1') THEN 
                  IF (DIR='1') THEN 
                      TMP<=TMP+1;
                      IF TMP="1100" THEN 
                            F<='1';
                         ELSE F<='0';
                       END IF;
                 ELSE 
                     TMP<=TMP-1;
                     IF TMP="0000" THEN
                        F<='1';
                        ELSE F<='0'; 
                     END IF;
                        END IF;                      
                  END IF;
         END IF;
   END PROCESS;

   COUNT<=TMP;
   CARRY<=F;


END ArchNumarator_12;

// VHDL entity DCD_7S, as the project stores it:
LIBRARY ieee;
USE ieee.std_logic_1164.all;

ENTITY DCD_7S IS
  PORT (
 A: IN STD_LOGIC_VECTOR(3 DOWNTO 0);
  	a_b_c_d_e_f_g: OUT STD_LOGIC_VECTOR(6 DOWNTO 0));
END DCD_7S;
ARCHITECTURE ArchDCD_7S OF DCD_7S IS
BEGIN

  a_b_c_d_e_f_g <=  "0000001" when A=x"0" else
				"1001111" when A=x"1" else
				"0010010" when A=x"2" else
				"0000110" when A=x"3" else
				"1001100" when A=x"4" else
				"0100100" when A=x"5" else
				"0100000" when A=x"6" else
				"0001111" when A=x"7" else
				"0000000" when A=x"8" else
				"0000100" when A=x"9" else
				"0001000" when A=x"A" else
				"1100000" when A=x"B" else
				"0110000" when A=x"C" else
				"1000010" when A=x"D" else
				"0110000" when A=x"E" else
				"1111111" when A=x"F" else
				"1111111";

END ArchDCD_7S;

// VHDL entity Numarator_inchidere_usa, as the project stores it:
LIBRARY ieee;
USE ieee.std_logic_1164.all;
USE IEEE.STD_LOGIC_UNSIGNED.ALL;

ENTITY Numarator_inchidere_usa IS
  PORT (
          CLK,RESET,EN: IN STD_LOGIC;
  		CARRY: OUT STD_LOGIC);
END Numarator_inchidere_usa;
ARCHITECTURE ArchNumarator_inchidere_usa OF Numarator_inchidere_usa IS
SIGNAL TMP: STD_LOGIC_VECTOR (1 DOWNTO 0):=(OTHERS => '0');
SHARED VARIABLE G : STD_LOGIC;
BEGIN

PROCESS(CLK,RESET)
    BEGIN
    IF RISING_EDGE(CLK) THEN 
      IF RESET='1' THEN TMP<="00";
        G:='0';
        END IF;
        IF (EN='1') THEN   
              IF TMP="11" THEN TMP<="00";
                  G:='1'; 
               ELSE 
                 TMP<=TMP+1;
              END IF;    
          END IF;
       END IF;
       CARRY<=G;
    END PROCESS;
    

END ArchNumarator_inchidere_usa;

// VHDL entity Numarator_3s, as the project stores it:
LIBRARY ieee;
USE ieee.std_logic_1164.all;
USE IEEE.STD_LOGIC_UNSIGNED.ALL;

ENTITY Numarator_3s IS
  PORT (CLK,EN: IN STD_LOGIC;
  		--Y: OUT STD_LOGIC_VECTOR(1 DOWNTO 0);
  		CARRY: OUT STD_LOGIC);
END Numarator_3s;
ARCHITECTURE ARCHNumarator_3s OF Numarator_3s IS

SIGNAL TMP: STD_LOGIC_VECTOR (1 DOWNTO 0):=(OTHERS => '0');
SIGNAL G : STD_LOGIC :='0';
BEGIN

    PROCESS(CLK)
    BEGIN
    IF RISING_EDGE(CLK) THEN 
     IF G='1' THEN G<='0';
     END IF;
        IF (EN='1') THEN   
              IF TMP="11" THEN TMP<="00";
                  G<='1'; 
               ELSE 
                 TMP<=TMP+1;
              END IF;    
          END IF;
       END IF;
    END PROCESS;
  CARRY<=G;

END ARCHNumarator_3s;

// VHDL entity Registru_de_memorare, as the project stores it:
LIBRARY ieee;
USE ieee.std_logic_1164.all;

ENTITY Registru_de_memorare IS
  PORT (Load: in std_logic;
          R: in std_logic; 
          En: in std_logic;
         reset: in std_logic_vector(3 downto 0);
  	    Q: in std_logic_vector(3 downto 0);
  	    Y: inout std_logic_vector(12 downto 0));
END Registru_de_memorare;
ARCHITECTURE ArchRegistru_de_memorare OF Registru_de_memorare IS
SIGNAL Y1:STD_LOGIC_VECTOR(12 DOWNTO 0):=(OTHERS=> '0');
BEGIN
   PROCESS(Load,En,R)
     BEGIN  
     if R='1' then 
	        CASE RESET IS 
	           WHEN "0000"=> Y1(0)<='0';
			  WHEN "0001"=> Y1(1)<='0';
			   WHEN "0010"=> Y1(2)<='0';
			   WHEN "0011"=> Y1(3)<='0';
			   WHEN "0100" => Y1(4)<='0';
			   WHEN "0101" => Y1(5)<='0';
			   WHEN "0110" => Y1(6)<='0';
			   WHEN "0111" => Y1(7)<='0';
			   WHEN "1000" => Y1(8)<='0';
			   WHEN "1001" => Y1(9)<='0';
			   WHEN "1010" => Y1(10)<='0';
			   WHEN "1011" => Y1(11)<='0';
			   WHEN OTHERS => Y1(12)<='0';
			   END CASE;
	end if;
         IF rising_edge(Load) THEN  
	     if en='1' then
	       CASE Q IS 
		        WHEN "0000"=> Y1(0)<='1';
			   WHEN "0001"=> Y1(1)<='1';
			   WHEN "0010"=> Y1(2)<='1';
			   WHEN "0011"=> Y1(3)<='1';
			   WHEN "0100" => Y1(4)<='1';
			   WHEN "0101" => Y1(5)<='1';
			   WHEN "0110" => Y1(6)<='1';
			   WHEN "0111" => Y1(7)<='1';
			   WHEN "1000" => Y1(8)<='1';
			   WHEN "1001" => Y1(9)<='1';
			   WHEN "1010" => Y1(10)<='1';
			   WHEN "1011" => Y1(11)<='1';
			   WHEN OTHERS => Y1(12)<='1';
	       END CASE;
	     end if;
         END IF;			
  END PROCESS;   
  Y<=Y1; 

END ArchRegistru_de_memorare;

// VHDL entity MUX_16_1, as the project stores it:
LIBRARY ieee;
USE ieee.std_logic_1164.all;

ENTITY MUX_16_1 IS
  PORT (C0,C1,C2,C3,C4,C5,C6,C7,C8,C9,C10,C11,C12,C13,C14,C15: in std_logic;
  		SEL: in std_logic_vector(3 downto 0);
          Y: out std_logic);
END MUX_16_1;

ARCHITECTURE ArchMux OF MUX_16_1 IS
BEGIN
	  with SEL select
	  Y<= C0 when "0000", 
		C1 when "0001",
		C2 when "0010",
		C3 when "0011",
		C4 when "0100",
		C5 when "0101",
		C6 when "0110",
		C7 WHEN "0111",
		C8 WHEN "1000",
		C9 WHEN "1001",
		C10 WHEN "1010",
		C11 WHEN "1011",
		C12 WHEN "1100",
		C13 WHEN "1101",
		C14 WHEN "1110",
		C15 WHEN OTHERS; 
END ArchMux;

// VHDL entity Poarta_or, as the project stores it:
LIBRARY ieee;
USE ieee.std_logic_1164.all;

ENTITY Poarta_or IS
  PORT (
A,B,C: IN STD_LOGIC;
        Y : OUT STD_LOGIC);
END Poarta_or;
ARCHITECTURE Archor OF Poarta_or IS
BEGIN

     Y<=A OR B OR C;
END Archor;

// VHDL entity AFISARE_ETAJE, as the project stores it:
LIBRARY ieee;
USE ieee.std_logic_1164.all;
USE ieee.numeric_std.ALL;

ENTITY AFISARE_ETAJE IS
  PORT (
         ETAJ: in std_logic_vector(3 downto 0);
  	    C1, C2: out std_logic_vector(3 downto 0)
       );
END AFISARE_ETAJE;

ARCHITECTURE TypeArchitecture OF AFISARE_ETAJE IS
SHARED VARIABLE N,C,D:INTEGER;
BEGIN
	PROCESS(ETAJ)
	begin 

		N:=to_integer(unsigned(ETAJ));
		C:= N / 10;
		D:= N mod 10;

		C1 <= std_logic_vector( to_unsigned(C, C1'length));
		C2 <= std_logic_vector( to_unsigned(D, C2'length));

	end process;

END TypeArchitecture;

// VHDL entity UNITATE_DE_CONTROL, as the project stores it:
LIBRARY ieee;
USE ieee.std_logic_1164.all;

ENTITY UNITATE_DE_CONTROL IS
  PORT (ETAJ:IN STD_LOGIC_VECTOR(3 DOWNTO 0);
        PERSOANA_IN_USA, GREUTEATE_DEPASITA, INTERIOR, EXTERIOR_SUS, EXTERIOR_JOS,OK,FARA_CERERI,CLK,RESET: IN STD_LOGIC;
        RESET_DIR: IN STD_LOGIC;
        DIR: OUT STD_LOGIC;
        ENABLE_INCHIDERE_USA, LOAD_REGISTRII, EN_INTERIOR, EN_EXTERIOR_SUS, EN_EXTERIOR_JOS: OUT STD_LOGIC;
        ETAJ_CERUT:OUT STD_LOGIC_VECTOR(3 DOWNTO 0)
        );
END UNITATE_DE_CONTROL;
ARCHITECTURE ARCHUnitate_de_control OF UNITATE_DE_CONTROL IS

SIGNAL EN_INCH: STD_LOGIC;
SIGNAL CONDITII_INDEPLINITE: STD_LOGIC:='0';
SIGNAL DIRECTIE: STD_LOGIC:='1';
SIGNAL INCH_DES: STD_LOGIC;

COMPONENT Poarta_NOR IS
  PORT (
        A,B,C,D,CLK: IN STD_LOGIC;
        Y : OUT STD_LOGIC
        );
END COMPONENT;

COMPONENT Numarator_USA_DESCHISA IS
  PORT (
          CLK,RESET: IN STD_LOGIC;
  		CARRY, DESCH_INCHIS: OUT STD_LOGIC);
END COMPONENT;

BEGIN

     C1:Numarator_USA_DESCHISA PORT MAP (CLK,RESET,EN_INCH,INCH_DES);
     C2:Poarta_NOR PORT MAP (PERSOANA_IN_USA, GREUTEATE_DEPASITA,INCH_DES,FARA_CERERI, CLK, CONDITII_INDEPLINITE);
     WITH ETAJ SELECT 
       ETAJ_CERUT<="0000" WHEN "0000" , 
                   "0001" WHEN "0001" ,
                   "0010" WHEN "0010" ,
                   "0011" WHEN "0011" ,
                   "0100" WHEN "0100" , 
                   "0101" WHEN "0101" , 
                   "0110" WHEN "0110" ,
                   "0111" WHEN "0111" ,
                   "1000" WHEN "1000" ,
                   "1001" WHEN "1001" ,
                   "1010" WHEN "1010" ,
                   "1011" WHEN "1011" ,
                   "1100" WHEN "1100" ,
                   "1101" WHEN "1101" ,
                   "1110" WHEN "1110",
                   "1111" WHEN OTHERS;
     EN_EXTERIOR_JOS<=EXTERIOR_JOS;
     EN_EXTERIOR_SUS<=EXTERIOR_SUS;
     EN_INTERIOR<=INTERIOR;
     LOAD_REGISTRII<=OK;
     ENABLE_INCHIDERE_USA<=CONDITII_INDEPLINITE;   
     PROCESS(RESET_DIR) 
     BEGIN
         IF RISING_EDGE(RESET_DIR) THEN
            DIRECTIE<='0';
               IF RISING_EDGE(RESET_DIR) THEN
                DIRECTIE<='1';
                END IF;
         END IF;
        DIR<=DIRECTIE;
     END PROCESS;
END ARCHUnitate_de_control;

LIBRARY ieee;
USE ieee.std_logic_1164.all;

ENTITY Poarta_NOR IS
  PORT (
        A,B,C,D,CLK: IN STD_LOGIC;
        Y : OUT STD_LOGIC);
END Poarta_NOR;
ARCHITECTURE ArchNOR OF Poarta_NOR IS
BEGIN
   PROCESS(CLK)
   BEGIN
    IF RISING_EDGE(CLK) THEN

     Y<=NOT(A OR B OR C OR D);
     END IF;

   END PROCESS;
END ArchNOR;

LIBRARY ieee;
USE ieee.std_logic_1164.all;
USE IEEE.STD_LOGIC_UNSIGNED.ALL;

ENTITY Numarator_USA_DESCHISA IS
  PORT (
          CLK,RESET: IN STD_LOGIC;
  		CARRY, DESCH_INCHIS: OUT STD_LOGIC);
END Numarator_USA_DESCHISA;
ARCHITECTURE ArchNumarator_USA_DESCHISA OF Numarator_USA_DESCHISA IS
SIGNAL TMP: STD_LOGIC_VECTOR (1 DOWNTO 0):=(OTHERS => '0');
SIGNAL G : STD_LOGIC;
SIGNAL I : STD_LOGIC;
BEGIN

PROCESS(CLK,RESET)
    BEGIN
    IF RISING_EDGE(CLK) THEN 
    IF RESET='1' THEN TMP<="00";
        G<='0';
        I<='1';
            END IF;
              IF TMP="11" THEN TMP<="00";
                  G<='1'; 
                  I<='0';
               ELSE 
                 TMP<=TMP+1;
              END IF;    
       END IF;
       CARRY<=G;
       DESCH_INCHIS<=I;
    END PROCESS;
    

END ArchNumarator_USA_DESCHISA;

// VHDL entity Poarta_NOR_3In_13B, as the project stores it:
LIBRARY ieee;
USE ieee.std_logic_1164.all;

ENTITY Poarta_NOR_3In_13B IS
  PORT (A,B,C:IN STD_LOGIC_VECTOR(12 DOWNTO 0);
     CLK:IN STD_LOGIC;
        Y: OUT STD_LOGIC);
END Poarta_NOR_3In_13B;
ARCHITECTURE TypeArchitecture OF Poarta_NOR_3In_13B IS
signal g: std_logic;
BEGIN
      PROCESS(CLK)
      BEGIN 
       IF RISING_EDGE(CLK) THEN
           Y<=NOT((A(12) OR B(12) OR C(12))OR(A(11) OR B(11) OR C(11))OR(A(10) OR B(10) OR C(10))OR(A(9) OR B(9) OR C(9))OR(A(8) OR B(8) OR C(8))OR(A(7) OR B(7) OR C(7))OR(A(6) OR B(6) OR C(6))OR(A(5) OR B(5) OR C(5))OR(A(4) OR B(4) OR C(4))OR(A(3) OR B(3) OR C(3))OR(A(2) OR B(2) OR C(2))OR(A(1) OR B(1) OR C(1))OR(A(0) OR B(0) OR C(0)));  
           END IF;  
           END PROCESS;


END TypeArchitecture;

// VHDL entity divizor_frecventa, as the project stores it:
--------------------------------------------------------------------------------
-- Project :
-- File    :
-- Autor   :
-- Date    :
--
--------------------------------------------------------------------------------
-- Description :
--
--------------------------------------------------------------------------------

LIBRARY ieee;
USE ieee.std_logic_1164.all;
USE ieee.std_logic_UNSIGNED.all;


ENTITY divizor_frecventa IS
  PORT (
  		Clk_100 : in std_logic;
  		Clk_1Hz: out std_logic
    );
END divizor_frecventa;

--------------------------------------------------------------------------------
--Complete your VHDL description below
--------------------------------------------------------------------------------

ARCHITECTURE TypeArchitecture OF divizor_frecventa IS

BEGIN

process(Clk_100)
variable nr:std_logic_vector (25 downto 0) := (others =>'0');
begin
	if Clk_100'event and Clk_100='1' then
	else nr:=nr+1;
	end if;
	Clk_1Hz <= nr(25);
end process; 

END TypeArchitecture;

// VHDL entity afisare, as the project stores it:
--------------------------------------------------------------------------------
-- Project :
-- File    :
-- Autor   :
-- Date    :
--
--------------------------------------------------------------------------------
-- Description :
--
--------------------------------------------------------------------------------

LIBRARY ieee;
USE ieee.std_logic_1164.all;

ENTITY afisare IS
  PORT (
  		clk_100,reset: in std_logic;
  		I0,I1: in std_logic_vector(3 downto 0);
  		anozi: out std_logic_vector( downto 0);
  		catozi :out std_logic_vector(6 downto 0)
    );
END afisare;

ARCHITECTURE TypeArchitecture OF afisare IS

	component nr_clk
	PORT (
  		clk_100,reset:in std_logic;
  		clk_16: out std_logic
    );
	end component;
	
	component reg_inel
	PORT (
  			Clk_16:in std_logic;
  			Y:out std_logic_vector (7 downto 0)
    );
	end component;

	component codif_prioritar
	 PORT (
  		Intrare: in std_logic_vector (7 downto 0);
  		Iesire : out std_logic
    );
	end component;

	component mux4
	  PORT (
 		Sel: in std_logic;
  		I0,I1: in std_logic_vector(3 downto 0);
  		Y: out std_logic_vector (3 downto 0)
    );
	end component;

	component hex_7seg
	 PORT (
		 hex_in: in std_logic_vector(3 downto 0);
  		a_b_c_d_e_f_g: out std_logic_vector(6 downto 0)
  		);
	end component;
    signal clk1: std_logic :='0';
    signal y: std_logic_vector(7 downto 0) := (others =>'0');
    signal sel: std_logic :='0';
    signal y_mux: std_logic_vector(3 downto 0) := (others =>'0');
BEGIN

	C1:nr_clk port map(clk_100,reset,clk1);
     C2: reg_inel port map(clk1,y);
     C3: codif_prioritar port map(y,sel);
     C4:mux4 port map(sel,I0,I1,y_mux);
     C5: hex_7seg port map(y_mux,catozi);
    anozi<=y;

END TypeArchitecture;


--div_clk
LIBRARY ieee;
USE ieee.std_logic_1164.all;
use ieee.std_logic_unsigned.all;

ENTITY nr_clk IS
  PORT (
  		clk_100,reset:in std_logic;
  		clk_16: out std_logic
    );
END nr_clk;


ARCHITECTURE arch_clk OF nr_clk IS
begin
process(clk_100)
variable nr: std_logic_vector(15 downto 0):=(others =>'0');
begin
	if rising_edge(clk_100) then nr:=nr+1;
	end if;
	clk_16<=nr(15);
	end process;
END arch_clk;

-- registru inel

LIBRARY ieee;
USE ieee.std_logic_1164.all;

ENTITY reg_inel IS
  PORT (
  			Clk_16:in std_logic;
  			Y:out std_logic_vector (3 downto 0)
    );
END reg_inel;

ARCHITECTURE arch_reg OF reg_inel IS
	signal A:std_logic_vector(3 downto 0) :=('0','1','0','0');
BEGIN

	process(Clk_16)
	begin
		if Clk_16'event and Clk_16='1' then
			A(3)<=A(2); A(2)<=A(3); A(1 downto 0)<="00";
		end if;
		Y<=A;
	end process;
END arch_reg;

-- codificator prioritar
LIBRARY ieee;
USE ieee.std_logic_1164.all;

ENTITY codif_prioritar IS
  PORT (
  		Intrare: in std_logic_vector (7 downto 0);
  		Iesire : out std_logic
    );
END codif_prioritar;


ARCHITECTURE arch_codif OF codif_prioritar IS
BEGIN
	process( Intrare)
	begin
		case Intrare is
		when ("10000000") => Iesire<=('0');
		when others => Iesire<=('1');
		end case;
	end process;
END arch_codif;

--mux4
LIBRARY ieee;
USE ieee.std_logic_1164.all;

ENTITY mux4 IS
  PORT (
 		Sel: in std_logic;
  		I0,I1: in std_logic_vector(3 downto 0);
  		Y: out std_logic_vector (3 downto 0)
    );
END mux4;

ARCHITECTURE archm OF mux4 IS
BEGIN
	with Sel select Y <=
	     I0 when '0',
		I1 when others;
END archm;

-- hex-7seg

LIBRARY ieee;
USE ieee.std_logic_1164.all;

ENTITY hex_7seg IS

  PORT (
 		hex_in: in std_logic_vector(3 downto 0);
  		a_b_c_d_e_f_g: out std_logic_vector(6 downto 0)
  		);

END hex_7seg;

ARCHITECTURE arch_hex OF hex_7seg IS

BEGIN

	a_b_c_d_e_f_g <= "1111110" when hex_in= x"0" else
				  "0110000" when hex_in= x"1" else
				  "1101101" when hex_in= x"2" else
				  "1111001" when hex_in= x"3" else
				  "0110011" when hex_in= x"4" else
				  "1011011" when hex_in= x"5" else
				  "1011111" when hex_in= x"6" else
				  "1110000" when hex_in= x"7" else
				  "1111111" when hex_in= x"8" else
				  "1111011" when hex_in= x"9" else
				  "1110111" when hex_in= x"A" else
				  "0011111" when hex_in= x"B" else
				  "1001110" when hex_in= x"C" else
				  "0111101" when hex_in= x"d" else
				  "1001111" when hex_in= x"E" else
				  "1000111" when hex_in= x"F" else
				  "0000000";

END arch_hex;
